# Fritzing sketch Guanto (saved by Fritzing 0.8.7b)
breadboards: 1

parts:
  Componente1 = Arduino Uno (Rev3)
  R1 = Basic Flex Resistor
  R2 = Basic Flex Resistor
  R3 = Basic Flex Resistor
  R4 = Basic Flex Resistor
  R5 = Basic Flex Resistor
  R7 = Resistor [tolerance=±5% resistance=10k package=THT]
  R8 = Resistor [tolerance=±5% resistance=10k package=THT]
  R10 = Resistor [tolerance=±5% resistance=10k package=THT]
  R11 = Resistor [tolerance=±5% resistance=10k package=THT]
  R12 = Resistor [tolerance=±5% resistance=10k package=THT]

nets:
  N1: Componente1.A0, R5.Pin_2, R12.Pin_1
  N2: Componente1.A1, R4.Pin_2, R7.Pin_1
  N3: Componente1.A2, R3.Pin_2, R10.Pin_1
  N4: Componente1.A3, R2.Pin_2, R8.Pin_1
  N5: Componente1.A4/SDA, R1.Pin_2, R11.Pin_1
  N6: Componente1.5V, R7.Pin_0, R8.Pin_0, R10.Pin_0, R11.Pin_0, R12.Pin_0
  N7: Componente1.GND, R1.pin_1, R2.pin_1, R3.pin_1, R4.pin_1, R5.pin_1

notes:
  Pollice
  Indice
  Medio
  Anulare
  Mignolo
  10 Kohm resistor
