# Fritzing sketch GuantoManoCompleto (saved by Fritzing 0.8.7b)
breadboards: 2

parts:
  Componente1 = Arduino Uno (Rev3)
  R1 = Basic Flex Resistor
  R2 = Basic Flex Resistor
  R3 = Basic Flex Resistor
  R4 = Basic Flex Resistor
  R5 = Basic Flex Resistor
  R7 = Resistor [tolerance=±5% resistance=10k package=THT]
  R8 = Resistor [tolerance=±5% resistance=10k package=THT]
  R10 = Resistor [tolerance=±5% resistance=10k package=THT]
  R11 = Resistor [tolerance=±5% resistance=10k package=THT]
  R12 = Resistor [tolerance=±5% resistance=10k package=THT]
  J14 = Basic Servo
  J15 = Basic Servo
  J16 = Basic Servo
  J17 = Basic Servo
  J18 = Basic Servo

nets:
  N1: Componente1.A0, R5.Pin_2, R12.Pin_1
  N2: Componente1.A1, R4.Pin_2, R7.Pin_1
  N3: Componente1.A2, R3.Pin_2, R10.Pin_1
  N4: Componente1.A3, R2.Pin_2, R8.Pin_1
  N5: Componente1.A4/SDA, R1.Pin_2, R11.Pin_1
  N6: Componente1.D9_PWM, J15.pulse
  N7: Componente1.D10_PWM/SS, J17.pulse
  N8: Componente1.D3_PWM, J16.pulse
  N9: Componente1.D5_PWM, J18.pulse
  N10: Componente1.D6_PWM, J14.pulse
  N11: Componente1.5V, R7.Pin_0, R8.Pin_0, R10.Pin_0, R11.Pin_0, R12.Pin_0
  N12: Componente1.GND, R1.pin_1, R2.pin_1, R3.pin_1, R4.pin_1, R5.pin_1
  GND: J14.gnd, J15.gnd, J16.gnd, J17.gnd, J18.gnd
  VCC: J14.vcc, J15.vcc, J16.vcc, J17.vcc, J18.vcc

notes:
  Pollice
  Indice
  Medio
  Anulare
  Mignolo
  10 Kohm resistor
  Alimentazione con alimentatore a tensione variabile impostato a 6V e 2,5A
