# Fritzing sketch Mano (saved by Fritzing 0.8.7b)
breadboards: 1

parts:
  Componente2 = Arduino Uno (Rev3)
  J9 = Basic Servo
  J10 = Basic Servo
  J11 = Basic Servo
  J12 = Basic Servo
  J13 = Basic Servo

nets:
  N1: Componente2.D9_PWM, J10.pulse
  N2: Componente2.D10_PWM/SS, J13.pulse
  N3: Componente2.D3_PWM, J12.pulse
  N4: Componente2.D5_PWM, J11.pulse
  N5: Componente2.D6_PWM, J9.pulse
  GND: Componente2.GND, J9.gnd, J10.gnd, J11.gnd, J12.gnd, J13.gnd
  VCC: J9.vcc, J10.vcc, J11.vcc, J12.vcc, J13.vcc
